// Logisim project PROCESSOR-dl.circ as structural Verilog: 50 circuits, main circuit main
module main (
  output [31:0] valM,
  output [31:0] Val_E,
  output [3:0] ALU_fun,
  output [2:0] CC,
  output [31:0] Val_A,
  output setCC,
  output [31:0] ALU_A,
  output [31:0] Val_B,
  output [15:0] valP,
  output [31:0] ALU_B,
  output [3:0] icode,
  output [3:0] ifun,
  output [3:0] rA,
  output [3:0] rB,
  output [31:0] valC,
  output [3:0] dstM,
  output [3:0] srcA,
  output [3:0] dstE,
  output [3:0] srcB,
  output [15:0] out_20,
  output [15:0] out_21
);

  wire clock_1_out, cond_1_cnd, fetch_unit_1_needregs, fetch_unit_1_needvalc, mem_control_1_read,
       mem_control_1_write;
  wire [2:0] alu_1_cc;
  wire [31:0] mem_addr_1_addr, mem_data_1_data;

  Clock clock_1 (.out(clock_1_out));
  Cond cond_1 (.CC(CC), .ifun(ifun), .cnd(cond_1_cnd));
  CC cc_1 (.in_1(setCC), .CC(alu_1_cc), .out_4(CC), .in_3(clock_1_out));
  setCC setcc_1 (.in_1(icode), .out_2(setCC));
  Mem_Control mem_control_1 (.icode(icode), .read(mem_control_1_read), .write(mem_control_1_write));
  Fetch_Unit fetch_unit_1 (
    .in_1(clock_1_out), .in_2(out_20), .icode(icode), .ifun(ifun), .needValC(fetch_unit_1_needvalc),
    .needRegs(fetch_unit_1_needregs), .regA(rA), .regB(rB), .valC(valC));
  Mem_Addr mem_addr_1 (.icode(icode), .valA(Val_A), .valE(Val_E), .addr(mem_addr_1_addr));
  ALU_A alu_a_1 (.icode(icode), .valC(valC), .valA(Val_A), .out_4(ALU_A));
  PC pc_1 (.in_1(clock_1_out), .in_2(out_21), .out_3(out_20));
  New_PC new_pc_1 (
    .icode(icode), .cnd(cond_1_cnd), .valP(valP), .out_7(out_21), .valC(valC), .valM(valM), .in_3(clock_1_out));
  Data_Memory data_memory_1 (
    .clk(clock_1_out), .read(mem_control_1_read), .write(mem_control_1_write), .addr(mem_addr_1_addr),
    .data(mem_data_1_data), .valE(valM));
  Mem_Data mem_data_1 (.icode(icode), .valA(Val_A), .valP(valP), .data(mem_data_1_data));
  ALU alu_1 (.ALU_A(ALU_A), .ALU_B(ALU_B), .ALU_fun(ALU_fun), .valE(Val_E), .CC(alu_1_cc), .in_4(clock_1_out));
  ALU_B alu_b_1 (.icode(icode), .valB(Val_B), .out_3(ALU_B));
  ALU_fun alu_fun_1 (.icode(icode), .ifun(ifun), .out_3(ALU_fun));
  PC_Increment pc_increment_1 (
    .needValC(fetch_unit_1_needvalc), .needRegs(fetch_unit_1_needregs), .in_3(out_20), .valP(valP));
  Register_File register_file_1 (
    .valE(Val_E), .valM(valM), .dstM(dstM), .dstE(dstE), .srcA(srcA), .in_6(clock_1_out), .srcB(srcB),
    .valA(Val_A), .valB(Val_B));
  dstE dste_1 (.icode(icode), .rB(rB), .out_3(dstE));
  dstM dstm_1 (.icode(icode), .rA(rA), .out_3(dstM));
  srcA srca_1 (.icode(icode), .rA(rA), .out_3(srcA));
  srcB srcb_1 (.icode(icode), .rB(rB), .out_3(srcB));
endmodule

module PC (
  input  in_1,
  input  [15:0] in_2,
  output [15:0] out_3
);

  wire cycle2_1_out_4, nor_1_out;
  wire [15:0] multiplexer_1_out, multiplexer_2_out, subtractor_1_out;
  wire [31:0] adder_1_out, register_1_q;

  cycle2 cycle2_1 (.in_1(in_1), .out_4(cycle2_1_out_4));  // open: out_2, out_3, out_5
  Adder #(.width(32)) adder_1 (.a(32'h1), .b(register_1_q), .out(adder_1_out));  // open: cin, cout
  Multiplexer #(.width(16)) multiplexer_1 (
    .in0(out_3), .in1(multiplexer_2_out), .out(multiplexer_1_out), .sel(cycle2_1_out_4));  // open: en
  Register_part #(.width(32)) register_1 (.D(adder_1_out), .Q(register_1_q), .clk(in_1));  // open: en, clr
  Register_part #(.width(16)) register_2 (.D(multiplexer_1_out), .Q(out_3), .clk(in_1));  // open: en, clr
  Subtractor #(.width(16)) subtractor_1 (.a(in_2), .b(16'h1), .out(subtractor_1_out));  // open: bin, bout
  Multiplexer #(.width(16)) multiplexer_2 (
    .in0(in_2), .in1(subtractor_1_out), .out(multiplexer_2_out), .sel(nor_1_out));  // open: en
  nor nor_1 (nor_1_out, register_1_q[0], register_1_q[1], register_1_q[2], register_1_q[3]);
endmodule

module cycle (
  input  in_1,
  output [2:0] out_2,
  output out_3,
  output out_4,
  output out_5
);

  wire and_1_out, and_3_out, and_4_out, not_1_out, not_2_out, not_3_out, not_4_out, not_5_out;
  wire [2:0] adder_1_out, multiplexer_1_out;

  Adder #(.width(3)) adder_1 (.a(out_2), .b(3'b001), .out(adder_1_out));  // open: cin, cout
  Multiplexer #(.width(3)) multiplexer_1 (
    .in0(adder_1_out), .in1(3'b000), .out(multiplexer_1_out), .sel(and_1_out));  // open: en
  Register_part #(.width(3)) register_1 (.D(multiplexer_1_out), .Q(out_2), .clk(in_1));  // open: en, clr
  not not_1 (not_1_out, out_2[0]);
  not not_2 (not_2_out, out_2[1]);
  not not_3 (not_3_out, out_2[2]);
  not not_4 (not_4_out, out_2[1]);
  not not_5 (not_5_out, out_2[0]);
  and and_1 (and_1_out, out_2[0], out_2[1], out_2[2]);
  and and_2 (out_3, not_1_out, not_2_out, not_3_out);
  and and_3 (and_3_out, out_2[0], not_4_out, out_2[2]);
  and and_4 (and_4_out, not_5_out, out_2[1], out_2[2]);
  and and_5 (out_4, out_2[0], out_2[1], out_2[2]);
  or or_1 (out_5, and_4_out, and_3_out);
endmodule

module Fetch_Unit (
  input  in_1,
  input  [15:0] in_2,
  output [3:0] icode,
  output [3:0] ifun,
  output [3:0] regA,
  output [3:0] regB,
  output [31:0] valC,
  output needValC,
  output needRegs
);

  wire cycle2_1_out_3, cycle2_1_out_5, demultiplexer_1_out0, demultiplexer_1_out1, demultiplexer_1_out2,
       demultiplexer_1_out3, demultiplexer_1_out4, demultiplexer_1_out5, fetch_demux_1_icode___ifun,
       fetch_demux_1_regs, fetch_demux_1_v1, fetch_demux_1_v2, fetch_demux_1_v3, fetch_demux_1_v4, not_1_out;
  wire [3:0] cycle2_1_out_2, multiplexer_4_out, multiplexer_5_out, multiplexer_6_out, multiplexer_7_out,
       values_logic_1_rega, values_logic_1_regb;
  wire [7:0] adder_1_out, demultiplexer_2_out0, demultiplexer_2_out1, demultiplexer_2_out2,
       demultiplexer_2_out3, demultiplexer_2_out4, demultiplexer_2_out5, multiplexer_1_out,
       multiplexer_2_out, multiplexer_3_out, multiplexer_8_out, multiplexer_9_out, multiplexer_10_out,
       multiplexer_11_out, ram_1_data, register_1_q, values_logic_1_out_10, values_logic_1_out_11,
       values_logic_1_out_12, values_logic_1_out_13;

  cycle2 cycle2_1 (.in_1(in_1), .out_2(cycle2_1_out_2), .out_3(cycle2_1_out_3), .out_5(cycle2_1_out_5));  // open: out_4
  Multiplexer #(.width(8)) multiplexer_1 (
    .in0(register_1_q), .in1(in_2[7:0]), .out(multiplexer_1_out), .sel(cycle2_1_out_3));  // open: en
  Demultiplexer #(.select(4)) demultiplexer_1 (
    .out0(demultiplexer_1_out0), .out1(demultiplexer_1_out1), .out2(demultiplexer_1_out2),
    .out3(demultiplexer_1_out3), .out4(demultiplexer_1_out4), .out5(demultiplexer_1_out5), .in(1'b1),
    .sel(cycle2_1_out_2));  // open: out6, out7, out8, out9, out10, out11, out12, out13, out14, out15, en
  Register_part register_1 (.D(multiplexer_3_out), .Q(register_1_q), .clk(in_1));  // open: en, clr
  RAM ram_1 (.addr(multiplexer_1_out), .data(ram_1_data), .clk(in_1));  // open: sel, ld, clr
  fetch_demux fetch_demux_1 (
    ._0(demultiplexer_1_out0), .in_2(demultiplexer_1_out1), .in_3(demultiplexer_1_out2),
    .in_4(demultiplexer_1_out3), .in_5(demultiplexer_1_out4), ._5(demultiplexer_1_out5),
    .need_Regs(needRegs), .icode___ifun(fetch_demux_1_icode___ifun), .regs(fetch_demux_1_regs),
    .v1(fetch_demux_1_v1), .v2(fetch_demux_1_v2), .v3(fetch_demux_1_v3), .v4(fetch_demux_1_v4));
  Demultiplexer #(.select(4), .width(8)) demultiplexer_2 (
    .out0(demultiplexer_2_out0), .out1(demultiplexer_2_out1), .out2(demultiplexer_2_out2),
    .out3(demultiplexer_2_out3), .out4(demultiplexer_2_out4), .out5(demultiplexer_2_out5), .in(ram_1_data),
    .sel(cycle2_1_out_2));  // open: out6, out7, out8, out9, out10, out11, out12, out13, out14, out15, en
  Multiplexer #(.width(8)) multiplexer_2 (
    .in0(register_1_q), .in1(in_2[7:0]), .out(multiplexer_2_out), .sel(cycle2_1_out_3));  // open: en
  Adder adder_1 (.a(multiplexer_2_out), .b(8'h1), .out(adder_1_out));  // open: cin, cout
  values_logic values_logic_1 (
    .in_1(demultiplexer_2_out1), .in_2(demultiplexer_2_out2), .in_3(demultiplexer_2_out3),
    .in_4(demultiplexer_2_out4), .in_5(demultiplexer_2_out5), .needValC(needValC), .needRegs(needRegs),
    .regA(values_logic_1_rega), .regB(values_logic_1_regb), .out_10(values_logic_1_out_10),
    .out_11(values_logic_1_out_11), .out_12(values_logic_1_out_12), .out_13(values_logic_1_out_13));
  Multiplexer #(.width(8)) multiplexer_3 (
    .in0(adder_1_out), .in1(register_1_q), .out(multiplexer_3_out), .sel(not_1_out));  // open: en
  not not_1 (not_1_out, cycle2_1_out_5);
  valsregslogic valsregslogic_1 (.in_1(icode), .valc(needValC), .regs(needRegs));
  Multiplexer #(.width(4)) multiplexer_4 (
    .in0(icode), .in1(demultiplexer_2_out0[7:4]), .out(multiplexer_4_out), .sel(fetch_demux_1_icode___ifun));  // open: en
  Multiplexer #(.width(4)) multiplexer_5 (
    .in0(ifun), .in1(demultiplexer_2_out0[3:0]), .out(multiplexer_5_out), .sel(fetch_demux_1_icode___ifun));  // open: en
  Multiplexer #(.width(4)) multiplexer_6 (
    .in0(regA), .in1(values_logic_1_rega), .out(multiplexer_6_out), .sel(fetch_demux_1_regs));  // open: en
  Multiplexer #(.width(4)) multiplexer_7 (
    .in0(regB), .in1(values_logic_1_regb), .out(multiplexer_7_out), .sel(fetch_demux_1_regs));  // open: en
  Multiplexer #(.width(8)) multiplexer_8 (
    .in0(valC[7:0]), .in1(values_logic_1_out_10), .out(multiplexer_8_out), .sel(fetch_demux_1_v1));  // open: en
  Multiplexer #(.width(8)) multiplexer_9 (
    .in0(valC[15:8]), .in1(values_logic_1_out_11), .out(multiplexer_9_out), .sel(fetch_demux_1_v2));  // open: en
  Multiplexer #(.width(8)) multiplexer_10 (
    .in0(valC[23:16]), .in1(values_logic_1_out_12), .out(multiplexer_10_out), .sel(fetch_demux_1_v3));  // open: en
  Multiplexer #(.width(8)) multiplexer_11 (
    .in0(valC[31:24]), .in1(values_logic_1_out_13), .out(multiplexer_11_out), .sel(fetch_demux_1_v4));  // open: en
  Register_part #(.width(4)) register_2 (.D(multiplexer_4_out), .Q(icode), .clk(in_1));  // open: en, clr
  Register_part #(.width(4)) register_3 (.D(multiplexer_5_out), .Q(ifun), .clk(in_1));  // open: en, clr
  Register_part #(.width(4)) register_4 (.D(multiplexer_6_out), .Q(regA), .clk(in_1));  // open: en, clr
  Register_part #(.width(4)) register_5 (.D(multiplexer_7_out), .Q(regB), .clk(in_1));  // open: en, clr
  Register_part register_6 (.D(multiplexer_8_out), .Q(valC[7:0]), .clk(in_1));  // open: en, clr
  Register_part register_7 (.D(multiplexer_9_out), .Q(valC[15:8]), .clk(in_1));  // open: en, clr
  Register_part register_8 (.D(multiplexer_10_out), .Q(valC[23:16]), .clk(in_1));  // open: en, clr
  Register_part register_9 (.D(multiplexer_11_out), .Q(valC[31:24]), .clk(in_1));  // open: en, clr
endmodule

module valsregslogic (
  input  [3:0] in_1,
  output valc,
  output regs
);

  wire and_1_out, and_2_out, and_3_out, and_4_out, and_5_out, and_6_out, not_1_out, not_2_out, not_3_out,
       not_4_out, not_5_out, not_6_out, not_7_out, not_8_out, not_9_out, not_10_out, not_11_out;

  not not_1 (not_1_out, in_1[3]);
  not not_2 (not_2_out, in_1[3]);
  not not_3 (not_3_out, in_1[1]);
  not not_4 (not_4_out, in_1[2]);
  not not_5 (not_5_out, in_1[1]);
  not not_6 (not_6_out, in_1[0]);
  not not_7 (not_7_out, in_1[2]);
  not not_8 (not_8_out, in_1[3]);
  not not_9 (not_9_out, in_1[1]);
  not not_10 (not_10_out, in_1[3]);
  not not_11 (not_11_out, in_1[0]);
  and and_1 (and_1_out, not_1_out, in_1[1], in_1[0]);
  and and_2 (and_2_out, not_2_out, in_1[2], not_3_out);
  and and_3 (and_3_out, in_1[3], not_4_out, not_5_out, not_6_out);
  and and_4 (and_4_out, not_7_out, in_1[1]);
  and and_5 (and_5_out, not_8_out, in_1[2], not_9_out);
  and and_6 (and_6_out, not_10_out, in_1[2], not_11_out);
  or or_1 (valc, and_1_out, and_2_out, and_3_out);
  or or_2 (regs, and_4_out, and_5_out, and_6_out);
endmodule

module PC_Increment (
  input  needValC,
  input  needRegs,
  input  [15:0] in_3,
  output [15:0] valP
);

  wire [15:0] adder_1_out, multiplexer_1_out, multiplexer_2_out;

  Multiplexer #(.width(16)) multiplexer_1 (
    .in0(16'h1), .in1(16'h2), .out(multiplexer_1_out), .sel(needRegs));  // open: en
  Adder #(.width(16)) adder_1 (.a(multiplexer_1_out), .b(in_3), .out(adder_1_out));  // open: cin, cout
  Multiplexer #(.width(16)) multiplexer_2 (
    .in0({16{1'b0}}), .in1(16'h4), .out(multiplexer_2_out), .sel(needValC));  // open: en
  Adder #(.width(16)) adder_2 (.a(multiplexer_2_out), .b(adder_1_out), .out(valP));  // open: cin, cout
endmodule

module New_PC (
  input  [3:0] icode,
  input  cnd,
  input  in_3,
  input  [31:0] valC,
  input  [31:0] valM,
  input  [15:0] valP,
  output [15:0] out_7
);

  wire and_1_out, and_2_out, and_3_out, and_4_out, and_5_out, j_call_ret_1_out, nor_1_out, not_1_out,
       not_2_out, not_3_out, not_4_out, not_5_out, not_6_out, not_7_out, or_1_out, or_2_out;
  wire [1:0] cc_mux_logic_1_s0;
  wire [15:0] multiplexer_1_out, register_1_q;

  j_call_ret j_call_ret_1 (.A(icode[3]), .B(icode[2]), .C(icode[1]), .D(icode[0]), .out(j_call_ret_1_out));
  nor nor_1 (nor_1_out, icode[3], icode[2], icode[1], icode[0]);
  or or_1 (or_1_out, icode[3], icode[2], icode[1], icode[0]);
  not not_1 (not_1_out, j_call_ret_1_out);
  not not_2 (not_2_out, icode[3]);
  not not_3 (not_3_out, icode[0]);
  not not_4 (not_4_out, icode[1]);
  not not_5 (not_5_out, icode[2]);
  not not_6 (not_6_out, icode[1]);
  not not_7 (not_7_out, icode[2]);
  and and_1 (and_1_out, icode[0], icode[1], icode[2], not_2_out);
  and and_2 (and_2_out, not_3_out, not_4_out, not_5_out, icode[3]);
  and and_3 (and_3_out, icode[0], not_6_out, not_7_out, icode[3]);
  and and_4 (and_4_out, or_1_out, not_1_out);
  and and_5 (and_5_out, and_1_out, cnd);
  or or_2 (or_2_out, and_5_out, and_2_out);
  cc_mux_logic cc_mux_logic_1 (
    .P(and_4_out), .C(or_2_out), .M(and_3_out), .s1(cc_mux_logic_1_s0[1]), .s0(cc_mux_logic_1_s0[0]));
  Multiplexer #(.select(2), .width(16)) multiplexer_1 (
    .in0(valP), .in1(valC[15:0]), .in2(valM[15:0]), .in3(valP), .out(multiplexer_1_out),
    .sel(cc_mux_logic_1_s0));  // open: en
  Multiplexer #(.width(16)) multiplexer_2 (
    .in0(multiplexer_1_out), .in1(register_1_q), .out(out_7), .sel(nor_1_out));  // open: en
  Register_part #(.width(16)) register_1 (.D(out_7), .Q(register_1_q), .clk(in_3));  // open: en, clr
endmodule

module rf (
  input  [31:0] valE,
  input  [3:0] srcA,
  input  [31:0] valM,
  input  [3:0] dstE,
  input  [3:0] dstM,
  input  [3:0] srcB,
  input  in_7,
  output [31:0] valA,
  output [31:0] valB
);

  wire decoder_1_d0, decoder_1_d1, decoder_1_d2, decoder_1_d5, decoder_1_d6, decoder_1_d7, decoder_2_d0,
       decoder_2_d1, decoder_2_d2, decoder_2_d3, decoder_2_d4, decoder_2_d5, decoder_2_d6, decoder_2_d7,
       undriven, undriven_2, undriven_3, undriven_4;
  wire [31:0] register_1_out_6, register_2_out_6, register_3_out_6, register_4_out_6, register_5_out_6,
       register_6_out_6, register_7_out_6, register_8_out_6, undriven_5;

  Decoder decoder_1 (
    .i3(dstE[3]), .i2(dstE[2]), .i1(dstE[1]), .i0(dstE[0]), .d7(decoder_1_d7), .d6(decoder_1_d6),
    .d5(decoder_1_d5), .d4(decoder_1_d5), .d2(decoder_1_d2), .d1(decoder_1_d1), .d0(decoder_1_d0));  // open: d3
  Decoder decoder_2 (
    .i3(dstM[3]), .i2(dstM[2]), .i1(dstM[1]), .i0(dstM[0]), .d7(decoder_2_d7), .d6(decoder_2_d6),
    .d5(decoder_2_d5), .d4(decoder_2_d4), .d3(decoder_2_d3), .d2(decoder_2_d2), .d1(decoder_2_d1),
    .d0(decoder_2_d0));
  Register register_1 (
    .valE(valE), .valM(valM), .M(decoder_2_d7), .in_4(decoder_1_d7), .clk(in_7), .out_6(register_1_out_6));
  Register register_2 (
    .valE(valE), .valM(valM), .M(decoder_2_d6), .in_4(decoder_1_d6), .clk(in_7), .out_6(register_2_out_6));
  Register register_3 (
    .valE(valE), .valM(valM), .M(decoder_2_d5), .in_4(undriven_4), .clk(in_7), .out_6(register_3_out_6));
  Register register_4 (
    .valE(valE), .valM(valM), .M(decoder_2_d4), .in_4(undriven_3), .clk(in_7), .out_6(register_4_out_6));
  Register register_5 (
    .valE(valE), .valM(valM), .M(decoder_2_d3), .in_4(undriven), .clk(in_7), .out_6(register_5_out_6));
  Register register_6 (.valE(valE), .valM(valM), .clk(in_7), .out_6(register_6_out_6));  // open: M, in_4
  Register register_7 (
    .valE(valE), .valM(undriven_5), .M(decoder_2_d1), .in_4(decoder_2_d2), .clk(in_7),
    .out_6(register_7_out_6));
  Register register_8 (
    .valE(valE), .valM(undriven_5), .M(decoder_2_d0), .in_4(undriven_2), .clk(in_7), .out_6(register_8_out_6));
  Multiplexer #(.select(4), .width(32)) multiplexer_1 (
    .in0(register_8_out_6), .in1(register_7_out_6), .in2(register_6_out_6), .in3(register_5_out_6),
    .in4(register_4_out_6), .in5(register_3_out_6), .in6(register_2_out_6), .in7(register_1_out_6),
    .out(valA), .sel(srcA));  // open: in8, in9, in10, in11, in12, in13, in14, in15, en
  Multiplexer #(.select(4), .width(32)) multiplexer_2 (
    .in0(register_8_out_6), .in1(register_7_out_6), .in2(register_6_out_6), .in3(register_5_out_6),
    .in4(register_4_out_6), .in5(register_3_out_6), .in6(register_2_out_6), .in7(register_1_out_6),
    .out(valB), .sel(srcB));  // open: in8, in9, in10, in11, in12, in13, in14, in15, en
endmodule

module Register (
  input  [31:0] valE,
  input  [31:0] valM,
  input  M,
  input  in_4,
  input  clk,
  output [31:0] out_6
);

  wire [31:0] multiplexer_1_out, multiplexer_2_out;

  Multiplexer #(.width(32)) multiplexer_1 (.in0(valE), .in1(valM), .out(multiplexer_1_out), .sel(M));  // open: en
  Register_part #(.width(32)) register_1 (.D(multiplexer_2_out), .Q(out_6), .clk(clk));  // open: en, clr
  Multiplexer #(.width(32)) multiplexer_2 (
    .in0(out_6), .in1(multiplexer_1_out), .out(multiplexer_2_out), .sel(in_4));  // open: en
endmodule

module Decoder (
  input  i3,
  input  i2,
  input  i1,
  input  i0,
  output d7,
  output d6,
  output d5,
  output d4,
  output d3,
  output d2,
  output d1,
  output d0
);

  wire not_1_out, not_2_out, not_3_out, not_4_out, not_5_out, not_6_out, not_7_out, not_8_out, not_9_out,
       not_10_out, not_11_out, not_12_out, not_13_out, not_14_out, not_15_out, not_16_out, not_17_out,
       not_18_out, not_19_out, not_20_out;

  not not_1 (not_1_out, i3);
  not not_2 (not_2_out, i3);
  not not_3 (not_3_out, i0);
  not not_4 (not_4_out, i3);
  not not_5 (not_5_out, i1);
  not not_6 (not_6_out, i3);
  not not_7 (not_7_out, i1);
  not not_8 (not_8_out, i0);
  not not_9 (not_9_out, i3);
  not not_10 (not_10_out, i2);
  not not_11 (not_11_out, i3);
  not not_12 (not_12_out, i2);
  not not_13 (not_13_out, i0);
  not not_14 (not_14_out, i3);
  not not_15 (not_15_out, i2);
  not not_16 (not_16_out, i1);
  not not_17 (not_17_out, i3);
  not not_18 (not_18_out, i2);
  not not_19 (not_19_out, i1);
  not not_20 (not_20_out, i0);
  and and_1 (d7, not_1_out, i2, i1, i0);
  and and_2 (d6, not_2_out, i2, i1, not_3_out);
  and and_3 (d5, not_4_out, i2, not_5_out, i0);
  and and_4 (d4, not_6_out, i2, not_7_out, not_8_out);
  and and_5 (d3, not_9_out, not_10_out, i1, i0);
  and and_6 (d2, not_11_out, not_12_out, i1, not_13_out);
  and and_7 (d1, not_14_out, not_15_out, not_16_out, i0);
  and and_8 (d0, not_17_out, not_18_out, not_19_out, not_20_out);
endmodule

module dstM (
  input  [3:0] icode,
  input  [3:0] rA,
  output [3:0] out_3
);

  Multiplexer #(.select(4), .width(4)) multiplexer_1 (
    .in0(4'b1111), .in1(4'b1111), .in2(4'b1111), .in3(4'b1111), .in4(4'b1111), .in5(rA), .in6(4'b1111),
    .in7(4'b1111), .in8(4'b1111), .in9(4'b1111), .in10(4'b1111), .in11(rA), .out(out_3), .sel(icode));  // open: in12, in13, in14, in15, en
endmodule

module dstE (
  input  [3:0] icode,
  input  [3:0] rB,
  output [3:0] out_3
);

  Multiplexer #(.select(4), .width(4)) multiplexer_1 (
    .in0(4'b1111), .in1(4'b1111), .in2(rB), .in3(rB), .in4(4'b1111), .in5(4'b1111), .in6(rB), .in7(4'b1111),
    .in8(4'b0100), .in9(4'b0100), .in10(4'b0100), .in11(4'b0100), .out(out_3), .sel(icode));  // open: in12, in13, in14, in15, en
endmodule

module srcA (
  input  [3:0] icode,
  input  [3:0] rA,
  output [3:0] out_3
);

  Multiplexer #(.select(4), .width(4)) multiplexer_1 (
    .in0(4'b1111), .in1(4'b1111), .in2(rA), .in3(4'b1111), .in4(rA), .in5(4'b1111), .in6(rA), .in7(4'b1111),
    .in8(4'b0100), .in9(4'b0100), .in10(rA), .in11(4'b0100), .out(out_3), .sel(icode));  // open: in12, in13, in14, in15, en
endmodule

module srcB (
  input  [3:0] icode,
  input  [3:0] rB,
  output [3:0] out_3
);

  Multiplexer #(.select(4), .width(4)) multiplexer_1 (
    .in0(4'b1111), .in1(4'b1111), .in2(4'b1111), .in3(4'b1111), .in4(rB), .in5(rB), .in6(rB), .in7(4'b1111),
    .in8(4'b1111), .in9(4'b1111), .in10(4'b0100), .in11(4'b1111), .out(out_3), .sel(icode));  // open: in12, in13, in14, in15, en
endmodule

module ALU_A (
  input  [3:0] icode,
  input  [31:0] valC,
  input  [31:0] valA,
  output [31:0] out_4
);

  Multiplexer #(.select(4), .width(32)) multiplexer_1 (
    .in0({32{1'b0}}), .in1({32{1'b0}}), .in2(valA), .in3(valC), .in4(valC), .in5(valC), .in6(valA),
    .in7({32{1'b0}}), .in8(valA), .in9(valA), .in10(32'hfffffffc), .in11(valA), .out(out_4), .sel(icode));  // open: in12, in13, in14, in15, en
endmodule

module ALU_B (
  input  [3:0] icode,
  input  [31:0] valB,
  output [31:0] out_3
);

  Multiplexer #(.select(4), .width(32)) multiplexer_1 (
    .in0({32{1'b0}}), .in1({32{1'b0}}), .in2({32{1'b0}}), .in3({32{1'b0}}), .in4(valB), .in5(valB),
    .in6(valB), .in7({32{1'b0}}), .in8(32'hfffffffc), .in9(32'h4), .in10(valB), .in11(32'h4), .out(out_3),
    .sel(icode));  // open: in12, in13, in14, in15, en
endmodule

module setCC (
  input  [3:0] in_1,
  output out_2
);

  wire not_1_out;

  not not_1 (not_1_out, in_1[3]);
  and and_1 (out_2, in_1[0], in_1[1], in_1[2], not_1_out);
endmodule

module ALU_fun (
  input  [3:0] icode,
  input  [3:0] ifun,
  output [3:0] out_3
);

  wire and_1_out, not_1_out;

  and and_1 (and_1_out, icode[1], icode[2], not_1_out);
  not not_1 (not_1_out, icode[3]);
  Multiplexer #(.width(4)) multiplexer_1 (.in0(4'b0000), .in1(ifun), .out(out_3), .sel(and_1_out));  // open: en
endmodule

module ALU (
  input  [31:0] ALU_A,
  input  [31:0] ALU_B,
  input  [3:0] ALU_fun,
  input  in_4,
  output [31:0] valE,
  output [2:0] CC
);

  wire adder_1_cout, alu_timer_1_out_2, or_1_out, subtractor_1_bout;
  wire [31:0] adder_1_out, and_1_out, multiplexer_1_out, multiplexer_2_out, subtractor_1_out, xor_1_out;

  Adder #(.width(32)) adder_1 (.a(ALU_A), .b(ALU_B), .out(adder_1_out), .cout(adder_1_cout));  // open: cin
  Subtractor #(.width(32)) subtractor_1 (
    .a(ALU_A), .b(ALU_B), .out(subtractor_1_out), .bout(subtractor_1_bout));  // open: bin
  or or_1 (or_1_out, adder_1_cout, subtractor_1_bout);
  assign and_1_out = ALU_A & ALU_B;  // AND_Gate and_1, 32 bits wide
  assign xor_1_out = ALU_A ^ ALU_B;  // XOR_Gate xor_1, 32 bits wide
  get_flags get_flags_1 (.valE(valE), .out(or_1_out), .out_3(CC));
  Multiplexer #(.select(4), .width(32)) multiplexer_1 (
    .in0(adder_1_out), .in1(subtractor_1_out), .in2(and_1_out), .in3(xor_1_out), .out(multiplexer_1_out),
    .sel(ALU_fun));  // open: in4, in5, in6, in7, in8, in9, in10, in11, in12, in13, in14, in15, en
  ALU_timer alu_timer_1 (.in_1(in_4), .out_2(alu_timer_1_out_2));
  Multiplexer #(.width(32)) multiplexer_2 (
    .in0(valE), .in1(multiplexer_1_out), .out(multiplexer_2_out), .sel(alu_timer_1_out_2));  // open: en
  Register_part #(.width(32)) register_1 (.D(multiplexer_2_out), .Q(valE), .clk(in_4));  // open: en, clr
endmodule

module values_logic (
  input  [7:0] in_1,
  input  [7:0] in_2,
  input  [7:0] in_3,
  input  [7:0] in_4,
  input  [7:0] in_5,
  input  needValC,
  input  needRegs,
  output [3:0] regA,
  output [3:0] regB,
  output [7:0] out_10,
  output [7:0] out_11,
  output [7:0] out_12,
  output [7:0] out_13
);

  Multiplexer #(.width(4)) multiplexer_1 (.in0(4'b1111), .in1(in_1[7:4]), .out(regA), .sel(needRegs));  // open: en
  Multiplexer #(.width(4)) multiplexer_2 (.in0(4'b1111), .in1(in_1[3:0]), .out(regB), .sel(needRegs));  // open: en
  Multiplexer #(.select(2), .width(8)) multiplexer_3 (
    .in0({8{1'b0}}), .in1({8{1'b0}}), .in2(in_1), .in3(in_2), .out(out_10), .sel({needValC, needRegs}));  // open: en
  Multiplexer #(.select(2), .width(8)) multiplexer_4 (
    .in0({8{1'b0}}), .in1({8{1'b0}}), .in2(in_2), .in3(in_3), .out(out_11), .sel({needValC, needRegs}));  // open: en
  Multiplexer #(.select(2), .width(8)) multiplexer_5 (
    .in0({8{1'b0}}), .in1({8{1'b0}}), .in2(in_3), .in3(in_4), .out(out_12), .sel({needValC, needRegs}));  // open: en
  Multiplexer #(.select(2), .width(8)) multiplexer_6 (
    .in0({8{1'b0}}), .in1({8{1'b0}}), .in2(in_4), .in3(in_5), .out(out_13), .sel({needValC, needRegs}));  // open: en
endmodule

module CC (
  input  in_1,
  input  [2:0] CC,
  input  in_3,
  output [2:0] out_4
);

  wire cc_timer_1_out_2;
  wire [2:0] multiplexer_1_out, multiplexer_2_out;

  Multiplexer #(.width(3)) multiplexer_1 (.in0(3'b000), .in1(CC), .out(multiplexer_1_out), .sel(in_1));  // open: en
  cc_timer cc_timer_1 (.in_1(in_3), .out_2(cc_timer_1_out_2));
  Multiplexer #(.width(3)) multiplexer_2 (
    .in0(out_4), .in1(multiplexer_1_out), .out(multiplexer_2_out), .sel(cc_timer_1_out_2));  // open: en
  Register_part #(.width(3)) register_1 (.D(multiplexer_2_out), .Q(out_4), .clk(in_3));  // open: en, clr
endmodule

module ALU_timer (
  input  in_1,
  output out_2
);

  wire and_1_out, not_1_out, not_2_out, not_3_out;
  wire [3:0] adder_1_out, multiplexer_1_out, register_1_q;

  Adder #(.width(4)) adder_1 (.a(register_1_q), .b(4'b0001), .out(adder_1_out));  // open: cin, cout
  Multiplexer #(.width(4)) multiplexer_1 (
    .in0(adder_1_out), .in1(4'b0000), .out(multiplexer_1_out), .sel(and_1_out));  // open: en
  Register_part #(.width(4)) register_1 (.D(multiplexer_1_out), .Q(register_1_q), .clk(in_1));  // open: en, clr
  not not_1 (not_1_out, register_1_q[2]);
  not not_2 (not_2_out, register_1_q[0]);
  not not_3 (not_3_out, register_1_q[3]);
  and and_1 (and_1_out, register_1_q[0], register_1_q[1], not_1_out, register_1_q[3]);
  and and_2 (out_2, not_2_out, register_1_q[1], register_1_q[2], not_3_out);
endmodule

module Register_File (
  input  [31:0] valE,
  input  [31:0] valM,
  input  [3:0] dstM,
  input  [3:0] dstE,
  input  [3:0] srcA,
  input  in_6,
  input  [3:0] srcB,
  output [31:0] valA,
  output [31:0] valB
);

  wire write_back_timing_1_mem, write_decode_1_r0, write_decode_1_r1, write_decode_1_r2, write_decode_1_r3,
       write_decode_1_r4, write_decode_1_r5, write_decode_1_r6, write_decode_1_r7, write_decode_2_r0,
       write_decode_2_r1, write_decode_2_r2, write_decode_2_r3, write_decode_2_r4, write_decode_2_r5,
       write_decode_2_r6, write_decode_2_r7;
  wire [31:0] controlled_buffer_1_out, controlled_buffer_2_out, reg_1_out_6, reg_2_out_6, reg_3_out_6,
       reg_4_out_6, reg_5_out_6, reg_6_out_6, reg_7_out_6, reg_8_out_6;

  write_back_timing write_back_timing_1 (.in_1(in_6), .mem(write_back_timing_1_mem));  // open: out_2, valE
  write_decode write_decode_1 (
    .dst3(dstM[3]), .dst2(dstM[2]), .dst1(dstM[1]), .dst0(dstM[0]), .r7(write_decode_1_r7),
    .r6(write_decode_1_r6), .r5(write_decode_1_r5), .r4(write_decode_1_r4), .r3(write_decode_1_r3),
    .r2(write_decode_1_r2), .r1(write_decode_1_r1), .r0(write_decode_1_r0));
  write_decode write_decode_2 (
    .dst3(dstE[3]), .dst2(dstE[2]), .dst1(dstE[1]), .dst0(dstE[0]), .r7(write_decode_2_r7),
    .r6(write_decode_2_r6), .r5(write_decode_2_r5), .r4(write_decode_2_r4), .r3(write_decode_2_r3),
    .r2(write_decode_2_r2), .r1(write_decode_2_r1), .r0(write_decode_2_r0));
  assign controlled_buffer_1_out = write_back_timing_1_mem ? valE : 32'bz;  // Controlled_Buffer controlled_buffer_1
  assign controlled_buffer_2_out = write_back_timing_1_mem ? valM : 32'bz;  // Controlled_Buffer controlled_buffer_2
  \reg  reg_1 (
    .valE(controlled_buffer_1_out), .valM(controlled_buffer_2_out), .M(write_decode_1_r7),
    .in_4(write_decode_2_r7), .clk(in_6), .out_6(reg_1_out_6));
  \reg  reg_2 (
    .valE(controlled_buffer_1_out), .valM(controlled_buffer_2_out), .M(write_decode_1_r6),
    .in_4(write_decode_2_r6), .clk(in_6), .out_6(reg_2_out_6));
  \reg  reg_3 (
    .valE(controlled_buffer_1_out), .valM(controlled_buffer_2_out), .M(write_decode_1_r5),
    .in_4(write_decode_2_r5), .clk(in_6), .out_6(reg_3_out_6));
  \reg  reg_4 (
    .valE(controlled_buffer_1_out), .valM(controlled_buffer_2_out), .M(write_decode_1_r4),
    .in_4(write_decode_2_r4), .clk(in_6), .out_6(reg_4_out_6));
  \reg  reg_5 (
    .valE(controlled_buffer_1_out), .valM(controlled_buffer_2_out), .M(write_decode_1_r3),
    .in_4(write_decode_2_r3), .clk(in_6), .out_6(reg_5_out_6));
  \reg  reg_6 (
    .valE(controlled_buffer_1_out), .valM(controlled_buffer_2_out), .M(write_decode_1_r2),
    .in_4(write_decode_2_r2), .clk(in_6), .out_6(reg_6_out_6));
  \reg  reg_7 (
    .valE(controlled_buffer_1_out), .valM(controlled_buffer_2_out), .M(write_decode_1_r1),
    .in_4(write_decode_2_r1), .clk(in_6), .out_6(reg_7_out_6));
  \reg  reg_8 (
    .valE(controlled_buffer_1_out), .valM(controlled_buffer_2_out), .M(write_decode_1_r0),
    .in_4(write_decode_2_r0), .clk(in_6), .out_6(reg_8_out_6));
  Multiplexer #(.select(3), .width(32)) multiplexer_1 (
    .in0(reg_8_out_6), .in1(reg_7_out_6), .in2(reg_6_out_6), .in3(reg_5_out_6), .in4(reg_4_out_6),
    .in5(reg_3_out_6), .in6(reg_2_out_6), .in7(reg_1_out_6), .out(valA), .sel(srcA[2:0]));  // open: en
  Multiplexer #(.select(3), .width(32)) multiplexer_2 (
    .in0(reg_8_out_6), .in1(reg_7_out_6), .in2(reg_6_out_6), .in3(reg_5_out_6), .in4(reg_4_out_6),
    .in5(reg_3_out_6), .in6(reg_7_out_6), .in7(reg_8_out_6), .out(valB), .sel(srcB[2:0]));  // open: en
endmodule

module reg_decoder (
  input  i2,
  input  i1,
  input  i0,
  output d7,
  output d6,
  output d5,
  output d4,
  output d3,
  output d2,
  output d1,
  output d0
);

  wire not_1_out, not_2_out, not_3_out, not_4_out, not_5_out, not_6_out, not_7_out, not_8_out, not_9_out,
       not_10_out, not_11_out, not_12_out;

  and and_1 (d7, i2, i1, i0);
  not not_1 (not_1_out, i0);
  not not_2 (not_2_out, i1);
  not not_3 (not_3_out, i1);
  not not_4 (not_4_out, i0);
  not not_5 (not_5_out, i2);
  not not_6 (not_6_out, i2);
  not not_7 (not_7_out, i0);
  not not_8 (not_8_out, i2);
  not not_9 (not_9_out, i1);
  not not_10 (not_10_out, i2);
  not not_11 (not_11_out, i1);
  not not_12 (not_12_out, i0);
  and and_2 (d6, i2, i1, not_1_out);
  and and_3 (d5, i2, not_2_out, i0);
  and and_4 (d4, i2, not_3_out, not_4_out);
  and and_5 (d3, not_5_out, i1, i0);
  and and_6 (d2, not_6_out, i1, not_7_out);
  and and_7 (d1, not_8_out, not_9_out, i0);
  and and_8 (d0, not_10_out, not_11_out, not_12_out);
endmodule

module \reg  (
  input  [31:0] valE,
  input  [31:0] valM,
  input  M,
  input  in_4,
  input  clk,
  output [31:0] out_6
);

  wire or_1_out;
  wire [31:0] multiplexer_1_out, multiplexer_2_out;

  Multiplexer #(.width(32)) multiplexer_1 (.in0(valE), .in1(valM), .out(multiplexer_1_out), .sel(M));  // open: en
  Multiplexer #(.width(32)) multiplexer_2 (
    .in0(out_6), .in1(multiplexer_1_out), .out(multiplexer_2_out), .sel(or_1_out));  // open: en
  or or_1 (or_1_out, M, in_4);
  Register_part #(.width(32)) register_1 (.D(multiplexer_2_out), .Q(out_6), .clk(clk));  // open: en, clr
endmodule

module Mem_Control (
  input  [3:0] icode,
  output read,
  output write
);

  wire and_1_out, and_2_out, and_3_out, and_4_out, not_1_out, not_2_out, not_3_out, not_4_out, not_5_out;

  not not_1 (not_1_out, icode[1]);
  not not_2 (not_2_out, icode[0]);
  not not_3 (not_3_out, icode[2]);
  not not_4 (not_4_out, icode[3]);
  not not_5 (not_5_out, icode[2]);
  and and_1 (and_1_out, icode[0], not_3_out, icode[3]);
  and and_2 (and_2_out, icode[0], not_1_out, icode[2], not_4_out);
  and and_3 (and_3_out, not_2_out, not_1_out, icode[2], not_4_out);
  and and_4 (and_4_out, not_2_out, not_5_out, icode[3]);
  or or_1 (read, and_1_out, and_2_out);
  or or_2 (write, and_3_out, and_4_out);
endmodule

module Mem_Addr (
  input  [3:0] icode,
  input  [31:0] valA,
  input  [31:0] valE,
  output [31:0] addr
);

  Multiplexer #(.select(4), .width(32)) multiplexer_1 (
    .in0({32{1'b0}}), .in1({32{1'b0}}), .in2({32{1'b0}}), .in3({32{1'b0}}), .in4(valE), .in5(valE),
    .in6({32{1'b0}}), .in7({32{1'b0}}), .in8(valE), .in9(valA), .in10(valE), .in11(valA), .out(addr),
    .sel(icode));  // open: in12, in13, in14, in15, en
endmodule

module Mem_Data (
  input  [3:0] icode,
  input  [31:0] valA,
  input  [15:0] valP,
  output [31:0] data
);

  Multiplexer #(.select(4), .width(32)) multiplexer_1 (
    .in0({32{1'b0}}), .in1({32{1'b0}}), .in2({32{1'b0}}), .in3({32{1'b0}}), .in4(valA), .in5({32{1'b0}}),
    .in6({32{1'b0}}), .in7({32{1'b0}}), .in8({{16{1'b0}}, valP}), .in9({32{1'b0}}), .in10(valA),
    .in11({32{1'b0}}), .out(data), .sel(icode));  // open: in12, in13, in14, in15, en
endmodule

module Data_Memory (
  input  clk,
  input  read,
  input  write,
  input  [31:0] addr,
  input  [31:0] data,
  output [31:0] valE
);

  wire and_1_out, and_2_out, and_3_out, and_4_out, mem_out_1_o0, mem_out_1_o1, mem_out_1_o2, mem_out_1_o3,
       mem_write_logic_1_out, nand_1_out, not_1_out;
  wire [3:0] cycle3_1_out_2;
  wire [7:0] demultiplexer_1_out7, demultiplexer_1_out8, demultiplexer_1_out9, demultiplexer_1_out10,
       get_mem_adds_1_out_2, get_mem_adds_1_out_3, get_mem_adds_1_out_4, multiplexer_1_out,
       multiplexer_2_out, multiplexer_3_out, multiplexer_4_out, multiplexer_5_out, multiplexer_6_out,
       ram_1_data;

  cycle3 cycle3_1 (.in_1(clk), .out_2(cycle3_1_out_2));
  mem_write_logic mem_write_logic_1 (
    .D(cycle3_1_out_2[3]), .C(cycle3_1_out_2[2]), .B(cycle3_1_out_2[1]), .A(cycle3_1_out_2[0]),
    .out(mem_write_logic_1_out));
  get_mem_adds get_mem_adds_1 (
    .in_1(addr[7:0]), .out_2(get_mem_adds_1_out_2), .out_3(get_mem_adds_1_out_3), .out_4(get_mem_adds_1_out_4));
  Multiplexer #(.select(4), .width(8)) multiplexer_1 (
    .in7(addr[7:0]), .in8(get_mem_adds_1_out_2), .in9(get_mem_adds_1_out_3), .in10(get_mem_adds_1_out_4),
    .out(multiplexer_1_out), .sel(cycle3_1_out_2));  // open: in0, in1, in2, in3, in4, in5, in6, in11, in12, in13, in14, in15, en
  RAM ram_1 (.addr(multiplexer_1_out), .data(ram_1_data), .clk(clk), .ld(nand_1_out));  // open: sel, clr
  nand nand_1 (nand_1_out, mem_write_logic_1_out, write);
  Multiplexer #(.select(4), .width(8)) multiplexer_2 (
    .in7(data[31:24]), .in8(data[23:16]), .in9(data[15:8]), .in10(data[7:0]), .out(multiplexer_2_out),
    .sel(cycle3_1_out_2));  // open: in0, in1, in2, in3, in4, in5, in6, in11, in12, in13, in14, in15, en
  not not_1 (not_1_out, nand_1_out);
  assign ram_1_data = not_1_out ? multiplexer_2_out : 8'bz;  // Controlled_Buffer controlled_buffer_1
  Demultiplexer #(.select(4), .width(8)) demultiplexer_1 (
    .out7(demultiplexer_1_out7), .out8(demultiplexer_1_out8), .out9(demultiplexer_1_out9),
    .out10(demultiplexer_1_out10), .in(ram_1_data), .sel(cycle3_1_out_2));  // open: out0, out1, out2, out3, out4, out5, out6, out11, out12, out13, out14, out15, en
  Multiplexer #(.width(8)) multiplexer_3 (
    .in0(valE[31:24]), .in1(demultiplexer_1_out7), .out(multiplexer_3_out), .sel(and_1_out));  // open: en
  mem_out mem_out_1 (
    .D(cycle3_1_out_2[3]), .C(cycle3_1_out_2[2]), .B(cycle3_1_out_2[1]), .A(cycle3_1_out_2[0]),
    .o3(mem_out_1_o3), .o2(mem_out_1_o2), .o1(mem_out_1_o1), .o0(mem_out_1_o0));
  Multiplexer #(.width(8)) multiplexer_4 (
    .in0(valE[23:16]), .in1(demultiplexer_1_out8), .out(multiplexer_4_out), .sel(and_2_out));  // open: en
  Multiplexer #(.width(8)) multiplexer_5 (
    .in0(valE[15:8]), .in1(demultiplexer_1_out9), .out(multiplexer_5_out), .sel(and_3_out));  // open: en
  Multiplexer #(.width(8)) multiplexer_6 (
    .in0(valE[7:0]), .in1(demultiplexer_1_out10), .out(multiplexer_6_out), .sel(and_4_out));  // open: en
  and and_1 (and_1_out, read, mem_out_1_o3);
  and and_2 (and_2_out, read, mem_out_1_o2);
  and and_3 (and_3_out, read, mem_out_1_o1);
  and and_4 (and_4_out, read, mem_out_1_o0);
  Register_part register_1 (.D(multiplexer_3_out), .Q(valE[31:24]), .clk(clk));  // open: en, clr
  Register_part register_2 (.D(multiplexer_4_out), .Q(valE[23:16]), .clk(clk));  // open: en, clr
  Register_part register_3 (.D(multiplexer_5_out), .Q(valE[15:8]), .clk(clk));  // open: en, clr
  Register_part register_4 (.D(multiplexer_6_out), .Q(valE[7:0]), .clk(clk));  // open: en, clr
endmodule

module cycle2 (
  input  in_1,
  output [3:0] out_2,
  output out_3,
  output out_4,
  output out_5
);

  wire and_1_out, not_1_out, not_2_out, not_3_out, not_4_out, not_5_out, not_6_out;
  wire [3:0] adder_1_out, multiplexer_1_out;

  Adder #(.width(4)) adder_1 (.a(out_2), .b(4'b0001), .out(adder_1_out));  // open: cin, cout
  Multiplexer #(.width(4)) multiplexer_1 (
    .in0(adder_1_out), .in1(4'b0000), .out(multiplexer_1_out), .sel(and_1_out));  // open: en
  Register_part #(.width(4)) register_1 (.D(multiplexer_1_out), .Q(out_2), .clk(in_1));  // open: en, clr
  not not_1 (not_1_out, out_2[2]);
  not not_2 (not_2_out, out_2[0]);
  not not_3 (not_3_out, out_2[1]);
  not not_4 (not_4_out, out_2[2]);
  not not_5 (not_5_out, out_2[3]);
  _0_to_4 u_0_to_4_1 (.D(out_2[3]), .C(out_2[2]), .B(out_2[1]), .A(out_2[0]), .O(out_5));
  and and_1 (and_1_out, out_2[0], out_2[1], not_1_out, out_2[3]);
  and and_2 (out_3, not_2_out, not_3_out, not_4_out, not_5_out);
  not not_6 (not_6_out, out_2[2]);
  and and_3 (out_4, out_2[0], out_2[1], not_6_out, out_2[3]);
endmodule

module cycle_logic (
  input  D,
  input  C,
  input  B,
  input  A,
  output O
);

  wire and_1_out, and_2_out, and_3_out, and_4_out, not_1_out, not_2_out, not_3_out, not_4_out, not_5_out,
       not_6_out;

  not not_1 (not_1_out, D);
  and and_1 (and_1_out, not_1_out, C, A);
  not not_2 (not_2_out, D);
  and and_2 (and_2_out, not_2_out, C, B);
  and and_3 (and_3_out, D, not_3_out, not_4_out);
  not not_3 (not_3_out, C);
  not not_4 (not_4_out, B);
  not not_5 (not_5_out, C);
  and and_4 (and_4_out, D, not_5_out, not_6_out);
  not not_6 (not_6_out, A);
  or or_1 (O, and_1_out, and_2_out, and_3_out, and_4_out);
endmodule

module cycle3 (
  input  in_1,
  output [3:0] out_2
);

  wire and_1_out, not_1_out;
  wire [3:0] adder_1_out, multiplexer_1_out;

  Adder #(.width(4)) adder_1 (.a(out_2), .b(4'b0001), .out(adder_1_out));  // open: cin, cout
  Multiplexer #(.width(4)) multiplexer_1 (
    .in0(adder_1_out), .in1(4'b0000), .out(multiplexer_1_out), .sel(and_1_out));  // open: en
  Register_part #(.width(4)) register_1 (.D(multiplexer_1_out), .Q(out_2), .clk(in_1));  // open: en, clr
  not not_1 (not_1_out, out_2[2]);
  and and_1 (and_1_out, out_2[0], out_2[1], not_1_out, out_2[3]);
endmodule

module write_logic (
  input  D,
  input  C,
  input  B,
  input  A,
  output w
);

  wire not_1_out;

  and and_1 (w, D, not_1_out);
  not not_1 (not_1_out, C);
endmodule

module PC_copy (
  input  in_1,
  input  [15:0] in_2,
  output [15:0] out_3
);

  wire cycle2_1_out_4, nor_1_out;
  wire [3:0] adder_1_out, register_1_q;
  wire [15:0] multiplexer_1_out, multiplexer_2_out, subtractor_1_out;

  cycle2 cycle2_1 (.in_1(in_1), .out_4(cycle2_1_out_4));  // open: out_2, out_3, out_5
  Adder #(.width(4)) adder_1 (.a(4'b0001), .b(register_1_q), .out(adder_1_out));  // open: cin, cout
  Multiplexer #(.width(16)) multiplexer_1 (
    .in0(out_3), .in1(multiplexer_2_out), .out(multiplexer_1_out), .sel(cycle2_1_out_4));  // open: en
  Register_part #(.width(4)) register_1 (.D(adder_1_out), .Q(register_1_q), .clk(in_1));  // open: en, clr
  Register_part #(.width(16)) register_2 (.D(multiplexer_1_out), .Q(out_3), .clk(in_1));  // open: en, clr
  Subtractor #(.width(16)) subtractor_1 (.a(in_2), .b(16'h1), .out(subtractor_1_out));  // open: bin, bout
  Multiplexer #(.width(16)) multiplexer_2 (
    .in0(in_2), .in1(subtractor_1_out), .out(multiplexer_2_out), .sel(nor_1_out));  // open: en
  nor nor_1 (nor_1_out, register_1_q[0], register_1_q[1], register_1_q[2], register_1_q[3]);
endmodule

module get_flags (
  input  [31:0] valE,
  input  out,
  output [2:0] out_3
);

  nor nor_1 (out_3[0], valE[0], valE[1], valE[2], valE[3], valE[4], valE[5], valE[6], valE[7], valE[8], valE[9], valE[10], valE[11], valE[12], valE[13], valE[14], valE[15], valE[16], valE[17], valE[18], valE[19], valE[20], valE[21], valE[22], valE[23], valE[24], valE[25], valE[26], valE[27], valE[28], valE[29], valE[30], valE[31]);

  assign out_3[2:1] = {out, valE[31]};
endmodule

module Cond (
  input  [2:0] CC,
  input  [3:0] ifun,
  output cnd
);

  wire and_1_out, not_1_out, not_2_out, not_3_out, or_1_out, xor_1_out;

  xor xor_1 (xor_1_out, CC[1], CC[2]);
  not not_1 (not_1_out, CC[0]);
  not not_2 (not_2_out, xor_1_out);
  or or_1 (or_1_out, CC[0], xor_1_out);
  and and_1 (and_1_out, not_2_out, not_1_out);
  not not_3 (not_3_out, CC[0]);
  Multiplexer #(.select(3)) multiplexer_1 (
    .in0(1'b0), .in1(or_1_out), .in2(xor_1_out), .in3(CC[0]), .in4(not_3_out), .in5(not_2_out),
    .in6(and_1_out), .out(cnd), .sel(ifun[2:0]));  // open: in7, en
endmodule

module j_call_ret (
  input  A,
  input  B,
  input  C,
  input  D,
  output out
);

  wire and_1_out, and_2_out, not_1_out, not_2_out, not_3_out;

  not not_1 (not_1_out, A);
  not not_2 (not_2_out, B);
  not not_3 (not_3_out, C);
  and and_1 (and_1_out, not_1_out, B, C, D);
  or or_1 (out, and_1_out, and_2_out);
  and and_2 (and_2_out, A, not_2_out, not_3_out);
endmodule

module cc_mux_logic (
  input  P,
  input  C,
  input  M,
  output s1,
  output s0
);

  wire and_1_out, and_2_out, and_3_out, and_4_out, not_1_out, not_2_out, not_3_out, not_4_out, not_5_out,
       not_6_out, not_7_out, not_8_out;

  not not_1 (not_1_out, P);
  not not_2 (not_2_out, C);
  not not_3 (not_3_out, C);
  not not_4 (not_4_out, M);
  not not_5 (not_5_out, P);
  not not_6 (not_6_out, M);
  not not_7 (not_7_out, C);
  not not_8 (not_8_out, M);
  and and_1 (and_1_out, not_1_out, not_2_out, M);
  and and_2 (and_2_out, P, not_3_out, not_4_out);
  and and_3 (and_3_out, not_5_out, C, not_6_out);
  and and_4 (and_4_out, P, not_7_out, not_8_out);
  or or_1 (s1, and_1_out, and_2_out);
  or or_2 (s0, and_3_out, and_4_out);
endmodule

module cycle_logic_2 (
  input  D,
  input  C,
  input  B,
  input  A,
  output out
);

  wire and_1_out, and_2_out, and_3_out, and_4_out, not_1_out, not_2_out, not_3_out, not_4_out, not_5_out,
       not_6_out;

  not not_1 (not_1_out, D);
  and and_1 (and_1_out, not_1_out, C, A);
  not not_2 (not_2_out, D);
  and and_2 (and_2_out, not_2_out, C, B);
  and and_3 (and_3_out, D, not_3_out, not_4_out);
  not not_3 (not_3_out, C);
  not not_4 (not_4_out, B);
  and and_4 (and_4_out, D, not_5_out, not_6_out);
  not not_5 (not_5_out, C);
  not not_6 (not_6_out, A);
  or or_1 (out, and_1_out, and_2_out, and_3_out, and_4_out);
endmodule

module _0_to_4 (
  input  D,
  input  C,
  input  B,
  input  A,
  output O
);

  wire and_1_out, and_2_out, not_1_out, not_2_out, not_3_out, not_4_out, not_5_out;

  not not_1 (not_1_out, D);
  and and_1 (and_1_out, not_1_out, not_2_out);
  not not_2 (not_2_out, C);
  not not_3 (not_3_out, D);
  not not_4 (not_4_out, B);
  and and_2 (and_2_out, not_3_out, not_4_out, not_5_out);
  not not_5 (not_5_out, A);
  or or_1 (O, and_1_out, and_2_out);
endmodule

module fetch_demux (
  input  _0,
  input  in_2,
  input  in_3,
  input  in_4,
  input  in_5,
  input  _5,
  input  need_Regs,
  output icode___ifun,
  output regs,
  output v1,
  output v2,
  output v3,
  output v4
);

  Demultiplexer demultiplexer_1 (.out1(regs), .in(in_2), .sel(need_Regs));  // open: out0, en
  Multiplexer multiplexer_1 (.in0(in_5), .in1(_5), .out(v4), .sel(need_Regs));  // open: en
  Multiplexer multiplexer_2 (.in0(in_2), .in1(in_3), .out(v1), .sel(need_Regs));  // open: en
  Multiplexer multiplexer_3 (.in0(in_4), .in1(in_5), .out(v3), .sel(need_Regs));  // open: en
  Multiplexer multiplexer_4 (.in0(in_3), .in1(in_4), .out(v2), .sel(need_Regs));  // open: en

  assign icode___ifun = _0;
endmodule

module write_back_timing (
  input  in_1,
  output [3:0] out_2,
  output mem,
  output valE
);

  wire and_1_out, not_1_out, not_2_out, not_3_out;
  wire [3:0] adder_1_out, multiplexer_1_out;

  Adder #(.width(4)) adder_1 (.a(out_2), .b(4'b0001), .out(adder_1_out));  // open: cin, cout
  Multiplexer #(.width(4)) multiplexer_1 (
    .in0(adder_1_out), .in1(4'b0000), .out(multiplexer_1_out), .sel(and_1_out));  // open: en
  Register_part #(.width(4)) register_1 (.D(multiplexer_1_out), .Q(out_2), .clk(in_1));  // open: en, clr
  not not_1 (not_1_out, out_2[2]);
  not not_2 (not_2_out, out_2[2]);
  not not_3 (not_3_out, out_2[3]);
  and and_1 (and_1_out, out_2[0], out_2[1], not_1_out, out_2[3]);
  and and_2 (mem, out_2[0], out_2[1], not_2_out, out_2[3]);
  and and_3 (valE, out_2[0], out_2[1], out_2[2], not_3_out);
endmodule

module Register_File_2 (
  input  [31:0] valE,
  input  [31:0] valM,
  input  [3:0] dstM,
  input  [3:0] dstE,
  input  in_5,
  input  [3:0] srcA,
  input  [3:0] srcB,
  output [31:0] valA,
  output [31:0] valB
);

  wire [31:0] register_1_q, register_2_q, register_3_q, register_4_q, register_5_q, register_6_q,
       register_7_q, register_8_q;

  Register_part #(.width(32)) register_1 (.Q(register_1_q), .clk(in_5));  // open: D, en, clr
  Register_part #(.width(32)) register_2 (.Q(register_2_q), .clk(in_5));  // open: D, en, clr
  Register_part #(.width(32)) register_3 (.Q(register_3_q), .clk(in_5));  // open: D, en, clr
  Register_part #(.width(32)) register_4 (.Q(register_4_q), .clk(in_5));  // open: D, en, clr
  Register_part #(.width(32)) register_5 (.Q(register_5_q), .clk(in_5));  // open: D, en, clr
  Register_part #(.width(32)) register_6 (.Q(register_6_q), .clk(in_5));  // open: D, en, clr
  Register_part #(.width(32)) register_7 (.Q(register_7_q), .clk(in_5));  // open: D, en, clr
  Register_part #(.width(32)) register_8 (.Q(register_8_q), .clk(in_5));  // open: D, en, clr
  Multiplexer #(.select(4), .width(32)) multiplexer_1 (
    .out(valA), .sel(srcA));  // open: in0, in1, in2, in3, in4, in5, in6, in7, in8, in9, in10, in11, in12, in13, in14, in15, en
  Multiplexer #(.select(4), .width(32)) multiplexer_2 (
    .in0(register_1_q), .in1(register_2_q), .in2(register_3_q), .in3(register_4_q), .in4(register_5_q),
    .in5(register_6_q), .in6(register_7_q), .in7(register_8_q), .out(valB), .sel(srcB));  // open: in8, in9, in10, in11, in12, in13, in14, in15, en
endmodule

module write_decode (
  input  dst3,
  input  dst2,
  input  dst1,
  input  dst0,
  output r7,
  output r6,
  output r5,
  output r4,
  output r3,
  output r2,
  output r1,
  output r0
);

  wire not_1_out, not_2_out, not_3_out, not_4_out, not_5_out, not_6_out, not_7_out, not_8_out, not_9_out,
       not_10_out, not_11_out, not_12_out, not_13_out, not_14_out, not_15_out, not_16_out, not_17_out,
       not_18_out, not_19_out, not_20_out;

  not not_1 (not_1_out, dst3);
  not not_2 (not_2_out, dst3);
  not not_3 (not_3_out, dst0);
  not not_4 (not_4_out, dst3);
  not not_5 (not_5_out, dst1);
  not not_6 (not_6_out, dst3);
  not not_7 (not_7_out, dst1);
  not not_8 (not_8_out, dst0);
  not not_9 (not_9_out, dst3);
  not not_10 (not_10_out, dst2);
  not not_11 (not_11_out, dst3);
  not not_12 (not_12_out, dst2);
  not not_13 (not_13_out, dst0);
  not not_14 (not_14_out, dst3);
  not not_15 (not_15_out, dst2);
  not not_16 (not_16_out, dst1);
  not not_17 (not_17_out, dst3);
  not not_18 (not_18_out, dst2);
  not not_19 (not_19_out, dst1);
  not not_20 (not_20_out, dst0);
  and and_1 (r7, not_1_out, dst2, dst1, dst0);
  and and_2 (r6, not_2_out, dst2, dst1, not_3_out);
  and and_3 (r5, not_4_out, dst2, not_5_out, dst0);
  and and_4 (r4, not_6_out, dst2, not_7_out, not_8_out);
  and and_5 (r3, not_9_out, not_10_out, dst1, dst0);
  and and_6 (r2, not_11_out, not_12_out, dst1, not_13_out);
  and and_7 (r1, not_14_out, not_15_out, not_16_out, dst0);
  and and_8 (r0, not_17_out, not_18_out, not_19_out, not_20_out);
endmodule

module new_pc_cycle (
  input  in_1,
  output [3:0] out_2,
  output out_3,
  output out_4,
  output out_5
);

  wire and_1_out, not_1_out, not_2_out, not_3_out, not_4_out;
  wire [3:0] adder_1_out, multiplexer_1_out;

  Adder #(.width(4)) adder_1 (.a(out_2), .b(4'b0001), .out(adder_1_out));  // open: cin, cout
  Multiplexer #(.width(4)) multiplexer_1 (
    .in0(adder_1_out), .in1(4'b0000), .out(multiplexer_1_out), .sel(and_1_out));  // open: en
  Register_part #(.width(4)) register_1 (.D(multiplexer_1_out), .Q(out_2), .clk(in_1));  // open: en, clr
  not not_1 (not_1_out, out_2[2]);
  not not_2 (not_2_out, out_2[0]);
  not not_3 (not_3_out, out_2[3]);
  _0_to_4 u_0_to_4_1 (.D(out_2[3]), .C(out_2[2]), .B(out_2[1]), .A(out_2[0]), .O(out_5));
  and and_1 (and_1_out, out_2[0], out_2[1], not_1_out, out_2[3]);
  and and_2 (out_3, not_2_out, out_2[1], out_2[2], not_3_out);
  not not_4 (not_4_out, out_2[2]);
  and and_3 (out_4, out_2[0], out_2[1], not_4_out, out_2[3]);
endmodule

module get_mem_adds (
  input  [7:0] in_1,
  output [7:0] out_2,
  output [7:0] out_3,
  output [7:0] out_4
);

  Adder adder_1 (.a(8'h1), .b(in_1), .out(out_2));  // open: cin, cout
  Adder adder_2 (.a(8'h1), .b(out_2), .out(out_3));  // open: cin, cout
  Adder adder_3 (.a(8'h1), .b(out_3), .out(out_4));  // open: cin, cout
endmodule

module mem_write_logic (
  input  D,
  input  C,
  input  B,
  input  A,
  output out
);

  wire and_1_out, and_2_out, and_3_out, not_1_out, not_2_out, not_3_out, not_4_out, not_5_out;

  not not_1 (not_1_out, D);
  not not_2 (not_2_out, C);
  not not_3 (not_3_out, B);
  not not_4 (not_4_out, C);
  not not_5 (not_5_out, A);
  and and_1 (and_1_out, not_1_out, C, B, A);
  and and_2 (and_2_out, D, not_2_out, not_3_out);
  or or_1 (out, and_1_out, and_2_out, and_3_out);
  and and_3 (and_3_out, D, not_4_out, not_5_out);
endmodule

module cc_timer (
  input  in_1,
  output out_2
);

  wire and_1_out, not_1_out, not_2_out, not_3_out;
  wire [3:0] adder_1_out, multiplexer_1_out, register_1_q;

  Adder #(.width(4)) adder_1 (.a(register_1_q), .b(4'b0001), .out(adder_1_out));  // open: cin, cout
  Multiplexer #(.width(4)) multiplexer_1 (
    .in0(adder_1_out), .in1(4'b0000), .out(multiplexer_1_out), .sel(and_1_out));  // open: en
  Register_part #(.width(4)) register_1 (.D(multiplexer_1_out), .Q(register_1_q), .clk(in_1));  // open: en, clr
  not not_1 (not_1_out, register_1_q[2]);
  not not_2 (not_2_out, register_1_q[0]);
  not not_3 (not_3_out, register_1_q[3]);
  and and_1 (and_1_out, register_1_q[0], register_1_q[1], not_1_out, register_1_q[3]);
  and and_2 (out_2, not_2_out, register_1_q[1], register_1_q[2], not_3_out);
endmodule

module read_logic (
  input  D,
  input  C,
  input  B,
  input  A,
  output out
);

  wire and_1_out, and_2_out, not_1_out, not_2_out;

  not not_1 (not_1_out, D);
  not not_2 (not_2_out, C);
  and and_1 (and_1_out, not_1_out, C, B, A);
  or or_1 (out, and_1_out, and_2_out);
  and and_2 (and_2_out, D, not_2_out);
endmodule

module mem_out (
  input  D,
  input  C,
  input  B,
  input  A,
  output o3,
  output o2,
  output o1,
  output o0
);

  wire not_1_out, not_2_out, not_3_out, not_4_out, not_5_out, not_6_out, not_7_out, not_8_out;

  not not_1 (not_1_out, D);
  not not_2 (not_2_out, C);
  not not_3 (not_3_out, B);
  not not_4 (not_4_out, A);
  not not_5 (not_5_out, C);
  not not_6 (not_6_out, B);
  not not_7 (not_7_out, C);
  not not_8 (not_8_out, A);
  and and_1 (o3, not_1_out, C, B, A);
  and and_2 (o2, D, not_2_out, not_3_out, not_4_out);
  and and_3 (o1, D, not_5_out, not_6_out, A);
  and and_4 (o0, D, not_7_out, B, not_8_out);
endmodule
